# Fritzing sketch scheme-sketch-fritzing (saved by Fritzing 0.9.5d)
breadboards: 1

parts:
  Arduino_Uno = Arduino Uno (Rev3)
  S1 = Pushbutton [package="[THT]"]
  R1 = Resistor [tolerance=±5% resistance=10k package=THT]
  LED1 = LED - 5mm [color="Red (633nm)" package="5 mm [THT]"]
  R2 = Resistor [tolerance=±5% resistance=220 package=THT]
  LED2 = LED - 5mm [color="Green (560nm)" package="5 mm [THT]"]
  R3 = Resistor [tolerance=±5% resistance=220 package=THT]
  Water_Level_Sensor = Water Level Sensor
  Relay = Keyes Relay [package=THT]

nets:
  N1: Arduino_Uno.A5/SCL, Water_Level_Sensor.SIG
  N2: Arduino_Uno.D8, Relay.power
  N3: Arduino_Uno.D12/MISO, R3.Pin_0
  N4: Arduino_Uno.D13/SCK, R2.Pin_0
  GND: Arduino_Uno.GND, R1.Pin_0, LED1.cathode, LED2.cathode, Water_Level_Sensor.GND, Relay.ground
  N5: Arduino_Uno.D2, S1.Pin_3, S1.Pin_4, R1.Pin_1
  N6: Arduino_Uno.D4, Relay.signal
  N7: Arduino_Uno.D7, Water_Level_Sensor.VCC
  N8: Arduino_Uno.5V, S1.Pin_1, S1.Pin_2
  N9: LED1.anode, R2.Pin_1
  N10: LED2.anode, R3.Pin_1

custom parts:
  Water Level Sensor: A water level sensor. This sensor operates at 3V to 5V. The Sig (signal) pin outputs an analogue signal that is in proportion to the amount of water in contact with the sensor.
  Keyes Relay: The Keyes 5V relay module is suitable for SCM development, home appliance control. It uses a 5V~12V TIL control signal which can control DC / AC signal.
